# Fritzing sketch weather_station (saved by Fritzing 1.0.4)

parts:
  Mod1 = Raspberry Pi Pico W
  LCD2 = LCD screen
  LCM1602_IIC2 = LCM1602 IIC [part_number="LCM1602 IIC" chip_label="LCM1602 IIC" package="DIP (Dual Inline) [THT]"]

nets:
  N1: Mod1.pin_1, LCM1602_IIC2.SDA
  N2: Mod1.pin_2, LCM1602_IIC2.SCL
  N3: Mod1.pin_38, Mod1.pin_42, LCM1602_IIC2.GND
  N4: Mod1.pin_40, LCM1602_IIC2.VCC
  N5: LCD2.DB3, LCM1602_IIC2.D3
  N6: LCD2.DB4, LCM1602_IIC2.D4
  N7: LCD2.DB5, LCM1602_IIC2.D5
  N8: LCD2.DB6, LCM1602_IIC2.D6
  N9: LCD2.DB7, LCM1602_IIC2.D7
  N10: LCD2.LED+, LCM1602_IIC2.A
  N11: LCD2.LED-, LCM1602_IIC2.K
  N12: LCM1602_IIC2.LED_A, LCM1602_IIC2.LED_B

custom parts:
  Raspberry Pi Pico W: Raspberry Pi Pico W. Based around the RP2040 microcontroller the Pico W is a low cost microcontroller device bringing Raspberry Pi quality, cost, and easy of use to the microcontroller space. The areas marked KEEPOUT in pcb silkscreen should not have traces running through them to avoid shorts on a soldered in module!
  LCM1602 IIC: I2C-Module to use a 1602 or 2004 LCD on with the wire.h libory Serial LCD Modul
